# Fritzing sketch fritzing_file (saved by Fritzing 0.9.3b)
breadboards: 2

parts:
  LED1 = LED - 5mm [color="Red (633nm)" package="5 mm [THT]"]
  LED2 = LED - 5mm [color="Red (633nm)" package="5 mm [THT]"]
  LED3 = LED - 5mm [color="Red (633nm)" package="5 mm [THT]"]
  LED4 = LED - 5mm [color="Red (633nm)" package="5 mm [THT]"]
  R1 = Resistor [tolerance=±5% resistance=220 package=THT]
  R2 = Resistor [tolerance=±5% resistance=220 package=THT]
  R3 = Resistor [tolerance=±5% resistance=220 package=THT]
  R4 = Resistor [tolerance=±5% resistance=220 package=THT]
  Power_plug1 = Power plug
  U1 = Voltage Regulator - 5V [package="TO220 [THT]"]
  R5 = Photocell (LDR) [package=THT]
  U2 = Voltage Regulator - 5V [package="TO220 [THT]"]
  R6 = Resistor [tolerance=±5% resistance=220 package=THT]
  C1 = Ceramic Capacitor [capacitance=100nF package="100 mil [THT, multilayer]"]
  ESP1 = ESP32-WROOM-32
  C2 = Ceramic Capacitor [capacitance=100nF package="100 mil [THT, multilayer]"]
  J1 = Basic Servo

nets:
  GND: LED1.cathode, LED2.cathode, LED3.cathode, LED4.cathode, Power_plug1.GND, U1.GND, U2.GND, R6.Pin_1, C1.1, ESP1.connector1, C2.1, J1.gnd
  N1: LED1.anode, R4.Pin_0
  N2: LED2.anode, R3.Pin_0
  N3: LED3.anode, R2.Pin_0
  N4: LED4.anode, R1.Pin_0
  N5: R1.Pin_1, ESP1.connector19
  N6: R2.Pin_1, ESP1.connector17
  N7: R3.Pin_1, ESP1.connector16
  N8: R4.Pin_1, ESP1.connector13
  N9: Power_plug1.VCC, U1.input_voltage, U2.input_voltage, C1.0, C2.0
  N10: U1.output_voltage, J1.vcc
  N11: R5.pin_0, ESP1.connector28
  N12: R5.pin_1, R6.Pin_0
  N13: U2.output_voltage, ESP1.connector2
  N14: ESP1.connector12, J1.pulse
